# Fritzing sketch 7 segment display  (saved by Fritzing 1.0.2b)
breadboards: 1

parts:
  IC1 = DIP - 40 pins [chip_label=IC package="DIP (Dual Inline) [THT]"]
  LED1 = 7-SEGMENT-4DIGIT-YOUNGSUN [package=7-segment-4digit-youngsun]
  R1 = Resistor [tolerance=±5% power=0.25W resistance=220 package=THT]
  R2 = Resistor [tolerance=±5% power=0.25W resistance=220 package=THT]

nets:
  N1: IC1.23, LED1.A
  N2: IC1.22, LED1.B
  N3: IC1.21, LED1.C
  N4: IC1.19, LED1.D
  N5: IC1.18, LED1.E
  N6: IC1.5, LED1.F
  N7: IC1.4, LED1.G
  N8: IC1.2, R2.Pin_0
  N9: IC1.15, R1.Pin_1
  N10: LED1.DIGB, R2.Pin_1
  N11: LED1.DIG1, R1.Pin_0

custom parts:
  DIP - 40 pins: A DIP stand-in part for whatever IC you want. With 40 pins on a 300mil dual inline package (DIP) footprint.
  7-SEGMENT-4DIGIT-YOUNGSUN: This is a part for the 4-Digit 7-segment LEDs from Young Sun. Different from the Digikey LEDs, all 16 pins are used. The LONGPADS Variant is used for a test jig, but you may like it because there is more pad to solder to. If you are concerned about routing space, the standard works just fine though.
