# Fritzing sketch matrix_direct (saved by Fritzing 1.0.2b)
breadboards: 1

parts:
  IC1 = DIP - 40 pins [chip_label=IC package="DIP (Dual Inline) [THT]"]
  Disp1 = 38mm 8x8 dot matrix column cathode led display with standard pcb pads
  R1 = Resistor [tolerance=±5% power=0.25W resistance=220 package=THT]
  R2 = Resistor [tolerance=±5% power=0.25W resistance=220 package=THT]
  R3 = Resistor [tolerance=±5% power=0.25W resistance=220 package=THT]
  R4 = Resistor [tolerance=±5% power=0.25W resistance=220 package=THT]

nets:
  N1: IC1.3.3V, R1.Pin_0, R2.Pin_0, R3.Pin_0, R4.Pin_0
  N2: IC1.GND, Disp1.pin_8, Disp1.pin_9, Disp1.pin_12, Disp1.pin_14
  N3: Disp1.pin_3, R1.Pin_1
  N4: Disp1.pin_4, R2.Pin_1
  N5: Disp1.pin_10, R4.Pin_1
  N6: Disp1.pin_13, R3.Pin_1

custom parts:
  DIP - 40 pins: A DIP stand-in part for whatever IC you want. With 40 pins on a 300mil dual inline package (DIP) footprint.
