# Fritzing sketch matrix_esp (saved by Fritzing 1.0.2b)
breadboards: 1

parts:
  IC2 = DIP - 40 pins [chip_label=IC package="DIP (Dual Inline) [THT]"]
  Disp2 = 38mm 8x8 dot matrix column cathode led display with standard pcb pads
  R5 = Resistor [tolerance=±5% power=0.25W resistance=220 package=THT]
  R6 = Resistor [tolerance=±5% power=0.25W resistance=220 package=THT]
  R7 = Resistor [tolerance=±5% power=0.25W resistance=220 package=THT]
  R8 = Resistor [tolerance=±5% power=0.25W resistance=220 package=THT]

nets:
  N1: IC2.23, R5.Pin_1
  N2: IC2.22, R6.Pin_1
  N3: IC2.21, R7.Pin_1
  N4: IC2.19, R8.Pin_1
  N5: IC2.18, Disp2.pin_9
  N6: IC2.5, Disp2.pin_14
  N7: IC2.4, Disp2.pin_8
  N8: IC2.2, Disp2.pin_12
  N9: Disp2.pin_3, R6.Pin_0
  N10: Disp2.pin_4, R7.Pin_0
  N11: Disp2.pin_10, R8.Pin_0
  N12: Disp2.pin_13, R5.Pin_0

custom parts:
  DIP - 40 pins: A DIP stand-in part for whatever IC you want. With 40 pins on a 300mil dual inline package (DIP) footprint.
