# Fritzing sketch matrix_esp_max7219_2 (saved by Fritzing 1.0.2b)
breadboards: 1

parts:
  IC2 = DIP - 40 pins [chip_label=IC package="DIP (Dual Inline) [THT]"]
  8x8_LED_Modul_mit_MAX1 = 8x8 LED Modul mit MAX7219 [package=THT]
  8x8_LED_Modul_mit_MAX2 = 8x8 LED Modul mit MAX7219 [package=THT]

nets:
  N1: IC2.3.3V, 8x8_LED_Modul_mit_MAX1.VCC_Eingang
  N2: IC2.GND, 8x8_LED_Modul_mit_MAX1.GND_Eingang
  N3: IC2.23, 8x8_LED_Modul_mit_MAX1.DIN_Eingang
  N4: IC2.22, 8x8_LED_Modul_mit_MAX1.CS_Eingang
  N5: IC2.21, 8x8_LED_Modul_mit_MAX1.CLK_Eingang
  N6: 8x8_LED_Modul_mit_MAX1.DOUT_Ausgang, 8x8_LED_Modul_mit_MAX2.DIN_Eingang
  N7: 8x8_LED_Modul_mit_MAX1.CS_Ausgang, 8x8_LED_Modul_mit_MAX2.CS_Eingang
  N8: 8x8_LED_Modul_mit_MAX1.CLK_Ausgang, 8x8_LED_Modul_mit_MAX2.CLK_Eingang

custom parts:
  DIP - 40 pins: A DIP stand-in part for whatever IC you want. With 40 pins on a 300mil dual inline package (DIP) footprint.
